# Fritzing sketch demo (saved by Fritzing 0.9.0b)
circuit board: 8.03832cm x 5.60299cm
breadboards: 1

parts:
  D2 = Rectifier Diode [part_number=1N4001 package="Melf DO-213 AB [SMD]"]
  U4 = 555 Timer [package="DIP8 [THT]"]
  0_01u1 = Capacitor [package=cap-pth-small2]
  LED2 = LEDs [package=led10mm]
  U5 = TRANSISTOR_NPN [package=to-92-ammo]
  1K = TRIMPOT [package=trimpot_pth_s3_lock]
  0_01u2 = Capacitor [package=cap-pth-small2]
  1K_2 = TRIMPOT [package=trimpot_pth_s3_lock]
  1_3K = Resistor [tolerance=±5% resistance=1k package="0603 [SMD]"]
  4_7K = Resistor [tolerance=±5% resistance=220 package="0805 [SMD]"]
  560 = Resistor [tolerance=±5% resistance=470 package="0805 [SMD]"]

nets:
  N1: D2.cathode, U4.Trigger, U4.Threshold, 0_01u1.1, 1_3K.Pin_1
  N2: D2.anode, U4.Discharge, 1K.CW, 560.Pin_1
  GND: U4.Ground, 0_01u1.2, U5.E, 0_01u2.2
  N3: U4.Output, 4_7K.Pin_0
  N4: U4.Reset, 1K_2.CCW
  N5: U4.Control_Voltage, 0_01u2.1
  5V: U4.Vcc_Supply_Voltage, LED2.A
  N6: LED2.C, U5.C
  N7: U5.B, 4_7K.Pin_1
  N8: 1K.CCW, 1K.WIPER, 1_3K.Pin_0
  N9: 1K_2.WIPER, 1K_2.CW, 560.Pin_0

notes:
  Pin4输入基带信号，Pin3输出已调信号，调节两个电位计可调节载波周期和占空比
